// Logisim project ALU.circ as structural Verilog: 1 circuit, main circuit main
module main (
  input  [3:0] L,
  input  [3:0] R,
  input  in_3,
  output [3:0] out_4
);

  wire [3:0] adder_1_out;

  Adder #(.width(4)) adder_1 (.a(L), .b(R), .out(adder_1_out), .cin(1'b0));  // open: cout
  Register #(.width(4), .trigger("high")) register_1 (.D(adder_1_out), .en(1'b1), .Q(out_4), .clk(in_3));  // open: clr
endmodule
