// Logisim project uControlHW.circ as structural Verilog: 1 circuit, main circuit main
module main (
  input  CLK,
  input  Reset,
  input  Z,
  output [6:0] Control_BUS
);

  wire L_I, not_1_out;
  wire [1:0] register_1_q, rom_1_data_3;
  wire [2:0] counter_1_q, register_2_q, rom_1_data_2;
  wire [6:0] rom_1_data;

  Multiplexer #(.select(2)) multiplexer_1 (
    .in0(1'b0), .in1(Z), .in2(1'b1), .out(L_I), .sel(register_1_q), .en(1'b1));  // open: in3
  not not_1 (not_1_out, L_I);
  Register #(.width(2)) register_1 (.D(rom_1_data_3), .Q(register_1_q), .clk(CLK));  // open: en, clr
  Register #(.width(3)) register_2 (.D(rom_1_data_2), .Q(register_2_q), .clk(CLK));  // open: en, clr
  Counter #(.width(3), .max('h7)) counter_1 (
    .load(L_I), .D(register_2_q), .count(not_1_out), .Q(counter_1_q), .clk(CLK), .clr(Reset));  // open: carry
  Register #(.width(7)) register_3 (.D(rom_1_data), .Q(Control_BUS), .clk(CLK));  // open: en, clr
  ROM #(.addrWidth(3), .dataWidth(12)) rom_1 (
    .addr(counter_1_q), .data({rom_1_data_3, rom_1_data_2, rom_1_data}), .sel(1'b1));

  // Notes on the sheet:
  //   contents of rom_1 (hex, n*v repeats v):
  //   6 40 38 500 1 a81
endmodule
