// Logisim project uP_ProcessingHardware.circ as structural Verilog: 1 circuit, main circuit main
module main (
  input  [3:0] Bus_IN,
  input  CLK,
  input  [6:0] in_3,
  output Z,
  output [3:0] Bus_Out
);

  wire [3:0] main_1_out_6, main_2_out_4, main_3_out_6, main_4_out_6, not_1_out;

  _4bit_register_main main_1 (.BUS_IN(Bus_IN), .L(in_3[1]), .D(1'b0), .C(1'b0), .out_6(main_1_out_6), .CLK(CLK));
  ALU_main main_2 (.in_3(in_3[3]), .out_4(main_2_out_4), .L(main_1_out_6), .R(main_3_out_6));
  assign Bus_Out = in_3[0] ? main_2_out_4 : 4'bz;  // Controlled_Buffer controlled_buffer_1
  _4bit_register_main main_3 (
    .BUS_IN(main_2_out_4), .L(in_3[5]), .D(1'b0), .C(in_3[2]), .out_6(main_3_out_6), .CLK(CLK));
  _4bit_register_main main_4 (.BUS_IN(Bus_IN), .L(in_3[6]), .D(in_3[4]), .C(1'b0), .out_6(main_4_out_6), .CLK(CLK));
  assign not_1_out = ~main_4_out_6;  // NOT_Gate not_1, 4 bits wide
  nand nand_1 (Z, not_1_out[3], not_1_out[2], not_1_out[1], not_1_out[0]);

  // Other names for the same wires on the sheet: C0 = in_3[0]; C1 = in_3[1]; C2 = in_3[2]; C3 = in_3[3]; C4 = in_3[4];
  //   C5 = in_3[5]; C6 = in_3[6]

  // Notes on the sheet:
  //   M
  //   R
  //   Q
endmodule
