// Logisim project 4bit register.circ as structural Verilog: 1 circuit, main circuit main
module main (
  input  [3:0] BUS_IN,
  input  CLK,
  input  L,
  input  D,
  input  C,
  output [3:0] out_6
);

  wire adder_1_out, adder_2_cout, adder_3_cout, adder_3_out, adder_4_cout, adder_4_out, main_2_p3, main_2_p6,
       priority_encoder_1_en_out;
  wire [1:0] Sel;

  Priority_Encoder #(.select(2)) priority_encoder_1 (
    .in0(L), .in1(D), .in2(C), .out(Sel), .en_out(priority_encoder_1_en_out), .en_in(1'b1));  // open: in3, gs
  Single_Bit_Cell_main main_1 (
    .Sel(Sel), .D0(BUS_IN[3]), .D1(adder_1_out), .D2(1'b0), .clk(CLK), .Out(out_6[3]));  // open: D3
  Adder #(.width(1)) adder_1 (.a(out_6[3]), .b(1'b1), .out(adder_1_out), .cin(adder_2_cout));  // open: cout
  // Single_Bit_Cell_main main_2: pin names not known; wires that end beside it: Sel, CLK, main_2_p3, BUS_IN[2], main_2_p3, main_2_p6, out_6[2], 1'b0
  Adder #(.width(1)) adder_2 (.a(out_6[2]), .b(1'b1), .out(main_2_p6), .cin(adder_3_cout), .cout(adder_2_cout));
  Single_Bit_Cell_main main_3 (
    .Sel(Sel), .D0(BUS_IN[1]), .D1(adder_3_out), .D2(1'b0), .clk(CLK), .Out(out_6[1]));  // open: D3
  Adder #(.width(1)) adder_3 (.a(out_6[1]), .b(1'b1), .out(adder_3_out), .cin(adder_4_cout), .cout(adder_3_cout));
  Single_Bit_Cell_main main_4 (
    .Sel(Sel), .D0(BUS_IN[0]), .D1(adder_4_out), .D2(1'b0), .clk(CLK), .Out(out_6[0]));  // open: D3
  Adder #(.width(1)) adder_4 (.a(out_6[0]), .b(1'b1), .out(adder_4_out), .cin(1'b0), .cout(adder_4_cout));

  // Notes on the sheet:
  //   D= Decrement
  //   L = Load
  //   C = Clear
  //   Register Function
endmodule
