// Logisim project Single_Bit_Cell.circ as structural Verilog: 1 circuit, main circuit main
module main (
  input  D0,
  input  D1,
  input  D2,
  input  D3,
  input  [1:0] Sel,
  input  clk,
  output Out
);

  wire multiplexer_1_out;

  Multiplexer #(.select(2)) multiplexer_1 (
    .in0(D0), .in1(D1), .in2(D2), .in3(D3), .out(multiplexer_1_out), .sel(Sel), .en(1'b1));
  D_Flip_Flop d_ff_1 (.clk(clk), .D(multiplexer_1_out), .Q(Out));  // open: Qn, preset, en, reset
endmodule
