// Logisim project uP.circ as structural Verilog: 1 circuit, main circuit main
module main (
  input  [3:0] in_1,
  input  in_2,
  input  in_3,
  output [3:0] out_4
);

  wire main_2_z;
  wire [6:0] main_1_control_bus;

  uControlHW_main main_1 (.CLK(in_3), .Reset(in_2), .Z(main_2_z), .Control_BUS(main_1_control_bus));
  uP_ProcessingHardware_main main_2 (
    .Bus_IN(in_1), .in_3(main_1_control_bus), .Bus_Out(out_4), .CLK(in_3), .Z(main_2_z));
endmodule
